// Logisim project ALU.circ as structural Verilog
module main (
  input  [31:0] A,
  input  [31:0] B,
  input  [3:0] CONTROL,
  output Zero,
  output [31:0] OUTPUT
);

  wire [31:0] addition_1_output, and_1_output, nor_1_out_3, not_1_out, or_1_output, setonlessthan_1_out_3,
       subtracion_1_output;

  AND and_1 (.A(A), .B(B), .OUTPUT(and_1_output));
  OR or_1 (.A(A), .B(B), .OUTPUT(or_1_output));
  Addition addition_1 (.A(A), .B(B), .OUTPUT(addition_1_output));  // open: Cin
  Subtracion subtracion_1 (.A(A), .B(B), .OUTPUT(subtracion_1_output));
  SETONLESSTHAN setonlessthan_1 (.A(A), .B(B), .out_3(setonlessthan_1_out_3));
  NOR nor_1 (.A(A), .B(B), .out_3(nor_1_out_3));
  assign not_1_out = ~OUTPUT;  // NOT_Gate not_1, 32 bits wide
  Multiplexer #(.select(4), .width(32), .enable("false")) multiplexer_1 (
    .in0(and_1_output), .in1(or_1_output), .in2(addition_1_output), .in5(subtracion_1_output),
    .in6(setonlessthan_1_out_3), .in11(nor_1_out_3), .out(OUTPUT), .sel(CONTROL));  // open: in3, in4, in7, in8, in9, in10, in12, in13, in14, in15
  and and_2 (Zero, not_1_out[0], not_1_out[1], not_1_out[2], not_1_out[3], not_1_out[4], not_1_out[5], not_1_out[6], not_1_out[7], not_1_out[8], not_1_out[9], not_1_out[10], not_1_out[11], not_1_out[12], not_1_out[13], not_1_out[14], not_1_out[15], not_1_out[16], not_1_out[17], not_1_out[18], not_1_out[19], not_1_out[20], not_1_out[21], not_1_out[22], not_1_out[23], not_1_out[24], not_1_out[25], not_1_out[26], not_1_out[27], not_1_out[28], not_1_out[29], not_1_out[30], not_1_out[31]);
endmodule

module Addition (
  input  [31:0] A,
  input  Cin,
  input  [31:0] B,
  output [31:0] OUTPUT
);

  Adder #(.width(32)) adder_1 (.a(A), .b(B), .out(OUTPUT), .cin(Cin));  // open: cout
endmodule

module Subtracion (
  input  [31:0] A,
  input  [31:0] B,
  output [31:0] OUTPUT
);

  wire [31:0] not_1_out;

  Adder #(.width(32)) adder_1 (.a(A), .b(not_1_out), .out(OUTPUT), .cin(1'b1));  // open: cout
  assign not_1_out = ~B;  // NOT_Gate not_1, 32 bits wide
endmodule

module AND (
  input  [31:0] A,
  input  [31:0] B,
  output [31:0] OUTPUT
);

  assign OUTPUT = A & B;  // AND_Gate and_1, 32 bits wide
endmodule

module OR (
  input  [31:0] A,
  input  [31:0] B,
  output [31:0] OUTPUT
);

  assign OUTPUT = A | B;  // OR_Gate or_1, 32 bits wide
endmodule

module SETONLESSTHAN (
  input  [31:0] A,
  input  [31:0] B,
  output [31:0] out_3
);

  wire comparator_1_lt;

  Comparator #(.width(32)) comparator_1 (.a(A), .b(B), .lt(comparator_1_lt));  // open: gt, eq
  Multiplexer #(.width(32), .enable("false")) multiplexer_1 (.in0(B), .in1(A), .out(out_3), .sel(comparator_1_lt));
endmodule

module NOR (
  input  [31:0] A,
  input  [31:0] B,
  output [31:0] out_3
);

  assign out_3 = ~(A | B);  // NOR_Gate nor_1, 32 bits wide
endmodule
