// Logisim project MIPS.circ as structural Verilog: 11 circuits, main circuit main
module main (
  output [31:0] out_1,
  output [31:0] out_2
);

  wire alu_final_1_zero, and_1_out, clock_1_out, instruction_memory_1_alusrc, instruction_memory_1_branch,
       instruction_memory_1_j, instruction_memory_1_memread, instruction_memory_1_memtoreg,
       instruction_memory_1_memwrite, instruction_memory_1_regdst, instruction_memory_1_regwrite;
  wire [1:0] instruction_memory_1_aluop;
  wire [4:0] instruction_memory_1_intruction, instruction_memory_1_intruction_2, instruction_memory_1_out_13,
       multiplexer_2_out;
  wire [15:0] instruction_memory_1_instruction;
  wire [25:0] instruction_memory_1_out_15;
  wire [31:0] adder_1_out, adder_2_out, alu_final_1_result, bit_extender_1_out, bit_extender_2_out,
       multiplexer_1_out, multiplexer_3_out, multiplexer_4_out, multiplexer_5_out, pc_1_instruccion,
       pc_1_out_4, Registers_read_data_1, Registers_read_data_2;

  Clock clock_1 (.out(clock_1_out));
  Multiplexer #(.width(32), .enable("false")) multiplexer_1 (
    .in0(multiplexer_4_out), .in1(bit_extender_1_out), .out(multiplexer_1_out), .sel(instruction_memory_1_j));
  PC pc_1 (.in_1(multiplexer_1_out), .clk(clock_1_out), .Instruccion(pc_1_instruccion), .out_4(pc_1_out_4));
  assign bit_extender_1_out = {{6{1'b0}}, instruction_memory_1_out_15};  // Bit_Extender bit_extender_1
  Instruction_Memory instruction_memory_1 (
    .Read_Adress(pc_1_out_4), .out_15(instruction_memory_1_out_15), .RegDst(instruction_memory_1_regdst),
    .Branch(instruction_memory_1_branch), .MemRead(instruction_memory_1_memread),
    .MemtoReg(instruction_memory_1_memtoreg), .ALUOp(instruction_memory_1_aluop),
    .MemWrite(instruction_memory_1_memwrite), .AluSrc(instruction_memory_1_alusrc),
    .RegWrite(instruction_memory_1_regwrite), .J(instruction_memory_1_j),
    .Intruction(instruction_memory_1_intruction), .Intruction_2(instruction_memory_1_intruction_2),
    .out_13(instruction_memory_1_out_13), .Instruction(instruction_memory_1_instruction));
  Adder #(.width(32)) adder_1 (.a(pc_1_instruccion), .b(32'h4), .out(adder_1_out));  // open: cin, cout
  Multiplexer #(.width(5), .enable("false")) multiplexer_2 (
    .in0(instruction_memory_1_intruction_2), .in1(instruction_memory_1_out_13), .out(multiplexer_2_out),
    .sel(instruction_memory_1_regdst));
  assign bit_extender_2_out = {{16{1'b0}}, instruction_memory_1_instruction};  // Bit_Extender bit_extender_2
  Register Registers (
    .Read_register1(instruction_memory_1_intruction), .Read_Register_2(instruction_memory_1_intruction_2),
    .Write_register(multiplexer_2_out), .Write_Data(multiplexer_5_out),
    .Reg_Write(instruction_memory_1_regwrite), .clck(clock_1_out), .out_7(out_2),
    .Read_data_1(Registers_read_data_1), .Read_Data_2(Registers_read_data_2));
  Multiplexer #(.width(32), .enable("false")) multiplexer_3 (
    .in0(Registers_read_data_2), .in1(bit_extender_2_out), .out(multiplexer_3_out),
    .sel(instruction_memory_1_alusrc));
  Adder #(.width(32)) adder_2 (.a(adder_1_out), .b(bit_extender_2_out), .out(adder_2_out));  // open: cin, cout
  ALU_final alu_final_1 (
    ._1(Registers_read_data_1), ._2(multiplexer_3_out), .Alu_op(instruction_memory_1_aluop),
    .funct(instruction_memory_1_instruction[5:0]), .Zero(alu_final_1_zero), .Result(alu_final_1_result));
  Multiplexer #(.width(32), .enable("false")) multiplexer_4 (
    .in0(adder_1_out), .in1(adder_2_out), .out(multiplexer_4_out), .sel(and_1_out));
  and and_1 (and_1_out, instruction_memory_1_branch, alu_final_1_zero);
  Data_Memory data_memory_1 (
    .Adress(alu_final_1_result), .Write_data(Registers_read_data_2), .clk(clock_1_out),
    .MemWrite(instruction_memory_1_memwrite), .MemRead(instruction_memory_1_memread), .out_6(out_1));
  Multiplexer #(.width(32), .enable("false")) multiplexer_5 (
    .in0(alu_final_1_result), .in1(out_1), .out(multiplexer_5_out), .sel(instruction_memory_1_memtoreg));
endmodule

module Register (
  input  Reg_Write,
  input  clck,
  input  [4:0] Read_register1,
  input  [4:0] Read_Register_2,
  input  [4:0] Write_register,
  input  [31:0] Write_Data,
  output [31:0] out_7,
  output [31:0] Read_data_1,
  output [31:0] Read_Data_2
);

  wire decoder_1_out0, decoder_1_out1, decoder_1_out2, decoder_1_out3, decoder_1_out4, decoder_1_out5,
       decoder_1_out6, decoder_1_out7, decoder_1_out8, decoder_1_out9, decoder_1_out10, decoder_1_out11,
       decoder_1_out12, decoder_1_out13, decoder_1_out14, decoder_1_out15, decoder_1_out16, decoder_1_out17,
       decoder_1_out18, decoder_1_out19, decoder_1_out20, decoder_1_out21, decoder_1_out22, decoder_1_out23,
       decoder_1_out24, decoder_1_out25, decoder_1_out26, decoder_1_out27, decoder_1_out28, decoder_1_out29,
       decoder_1_out30, decoder_1_out31;
  wire [31:0] register_2_q, register_3_q, register_4_q, register_5_q, register_6_q, register_7_q,
       register_8_q, register_9_q, register_10_q, register_11_q, register_12_q, register_13_q, register_14_q,
       register_15_q, register_16_q, register_17_q, register_18_q, register_19_q, register_20_q,
       register_21_q, register_22_q, register_23_q, register_24_q, register_25_q, register_26_q,
       register_27_q, register_28_q, register_29_q, register_30_q, register_31_q, register_32_q;

  Decoder #(.select(5), .disabled(0)) decoder_1 (
    .out0(decoder_1_out0), .out1(decoder_1_out1), .out2(decoder_1_out2), .out3(decoder_1_out3),
    .out4(decoder_1_out4), .out5(decoder_1_out5), .out6(decoder_1_out6), .out7(decoder_1_out7),
    .out8(decoder_1_out8), .out9(decoder_1_out9), .out10(decoder_1_out10), .out11(decoder_1_out11),
    .out12(decoder_1_out12), .out13(decoder_1_out13), .out14(decoder_1_out14), .out15(decoder_1_out15),
    .out16(decoder_1_out16), .out17(decoder_1_out17), .out18(decoder_1_out18), .out19(decoder_1_out19),
    .out20(decoder_1_out20), .out21(decoder_1_out21), .out22(decoder_1_out22), .out23(decoder_1_out23),
    .out24(decoder_1_out24), .out25(decoder_1_out25), .out26(decoder_1_out26), .out27(decoder_1_out27),
    .out28(decoder_1_out28), .out29(decoder_1_out29), .out30(decoder_1_out30), .out31(decoder_1_out31),
    .sel(Write_register), .en(Reg_Write));
  Register_part #(.width(32)) register_1 (.D(Write_Data), .en(decoder_1_out0), .Q(out_7), .clk(clck));  // open: clr
  Register_part #(.width(32)) register_2 (
    .D(Write_Data), .en(decoder_1_out1), .Q(register_2_q), .clk(clck));  // open: clr
  Register_part #(.width(32)) register_3 (
    .D(Write_Data), .en(decoder_1_out2), .Q(register_3_q), .clk(clck));  // open: clr
  Register_part #(.width(32)) register_4 (
    .D(Write_Data), .en(decoder_1_out3), .Q(register_4_q), .clk(clck));  // open: clr
  Register_part #(.width(32)) register_5 (
    .D(Write_Data), .en(decoder_1_out4), .Q(register_5_q), .clk(clck));  // open: clr
  Register_part #(.width(32)) register_6 (
    .D(Write_Data), .en(decoder_1_out5), .Q(register_6_q), .clk(clck));  // open: clr
  Register_part #(.width(32)) register_7 (
    .D(Write_Data), .en(decoder_1_out6), .Q(register_7_q), .clk(clck));  // open: clr
  Register_part #(.width(32)) register_8 (
    .D(Write_Data), .en(decoder_1_out7), .Q(register_8_q), .clk(clck));  // open: clr
  Register_part #(.width(32)) register_9 (
    .D(Write_Data), .en(decoder_1_out8), .Q(register_9_q), .clk(clck));  // open: clr
  Register_part #(.width(32)) register_10 (
    .D(Write_Data), .en(decoder_1_out9), .Q(register_10_q), .clk(clck));  // open: clr
  Register_part #(.width(32)) register_11 (
    .D(Write_Data), .en(decoder_1_out10), .Q(register_11_q), .clk(clck));  // open: clr
  Register_part #(.width(32)) register_12 (
    .D(Write_Data), .en(decoder_1_out11), .Q(register_12_q), .clk(clck));  // open: clr
  Register_part #(.width(32)) register_13 (
    .D(Write_Data), .en(decoder_1_out12), .Q(register_13_q), .clk(clck));  // open: clr
  Register_part #(.width(32)) register_14 (
    .D(Write_Data), .en(decoder_1_out13), .Q(register_14_q), .clk(clck));  // open: clr
  Register_part #(.width(32)) register_15 (
    .D(Write_Data), .en(decoder_1_out14), .Q(register_15_q), .clk(clck));  // open: clr
  Register_part #(.width(32)) register_16 (
    .D(Write_Data), .en(decoder_1_out15), .Q(register_16_q), .clk(clck));  // open: clr
  Register_part #(.width(32)) register_17 (
    .D(Write_Data), .en(decoder_1_out16), .Q(register_17_q), .clk(clck));  // open: clr
  Register_part #(.width(32)) register_18 (
    .D(Write_Data), .en(decoder_1_out17), .Q(register_18_q), .clk(clck));  // open: clr
  Register_part #(.width(32)) register_19 (
    .D(Write_Data), .en(decoder_1_out18), .Q(register_19_q), .clk(clck));  // open: clr
  Register_part #(.width(32)) register_20 (
    .D(Write_Data), .en(decoder_1_out19), .Q(register_20_q), .clk(clck));  // open: clr
  Register_part #(.width(32)) register_21 (
    .D(Write_Data), .en(decoder_1_out20), .Q(register_21_q), .clk(clck));  // open: clr
  Register_part #(.width(32)) register_22 (
    .D(Write_Data), .en(decoder_1_out21), .Q(register_22_q), .clk(clck));  // open: clr
  Register_part #(.width(32)) register_23 (
    .D(Write_Data), .en(decoder_1_out22), .Q(register_23_q), .clk(clck));  // open: clr
  Register_part #(.width(32)) register_24 (
    .D(Write_Data), .en(decoder_1_out23), .Q(register_24_q), .clk(clck));  // open: clr
  Register_part #(.width(32)) register_25 (
    .D(Write_Data), .en(decoder_1_out24), .Q(register_25_q), .clk(clck));  // open: clr
  Register_part #(.width(32)) register_26 (
    .D(Write_Data), .en(decoder_1_out25), .Q(register_26_q), .clk(clck));  // open: clr
  Register_part #(.width(32)) register_27 (
    .D(Write_Data), .en(decoder_1_out26), .Q(register_27_q), .clk(clck));  // open: clr
  Register_part #(.width(32)) register_28 (
    .D(Write_Data), .en(decoder_1_out27), .Q(register_28_q), .clk(clck));  // open: clr
  Register_part #(.width(32)) register_29 (
    .D(Write_Data), .en(decoder_1_out28), .Q(register_29_q), .clk(clck));  // open: clr
  Register_part #(.width(32)) register_30 (
    .D(Write_Data), .en(decoder_1_out29), .Q(register_30_q), .clk(clck));  // open: clr
  Register_part #(.width(32)) register_31 (
    .D(Write_Data), .en(decoder_1_out30), .Q(register_31_q), .clk(clck));  // open: clr
  Register_part #(.width(32)) register_32 (
    .D(Write_Data), .en(decoder_1_out31), .Q(register_32_q), .clk(clck));  // open: clr
  Multiplexer #(.select(5), .width(32), .enable("false")) multiplexer_1 (
    .in0(out_7), .in1(register_2_q), .in2(register_3_q), .in3(register_4_q), .in4(register_5_q),
    .in5(register_6_q), .in6(register_7_q), .in7(register_8_q), .in8(register_9_q), .in9(register_10_q),
    .in10(register_11_q), .in11(register_12_q), .in12(register_13_q), .in13(register_14_q),
    .in14(register_15_q), .in15(register_16_q), .in16(register_17_q), .in17(register_18_q),
    .in18(register_19_q), .in19(register_20_q), .in20(register_21_q), .in21(register_22_q),
    .in22(register_23_q), .in23(register_24_q), .in24(register_25_q), .in25(register_26_q),
    .in26(register_27_q), .in27(register_28_q), .in28(register_29_q), .in29(register_30_q),
    .in30(register_31_q), .in31(register_32_q), .out(Read_data_1), .sel(Read_register1));
  Multiplexer #(.select(5), .width(32), .enable("false")) multiplexer_2 (
    .in0(out_7), .in1(register_2_q), .in2(register_3_q), .in3(register_4_q), .in4(register_5_q),
    .in5(register_6_q), .in6(register_7_q), .in7(register_8_q), .in8(register_9_q), .in9(register_10_q),
    .in10(register_11_q), .in11(register_12_q), .in12(register_13_q), .in13(register_14_q),
    .in14(register_15_q), .in15(register_16_q), .in16(register_17_q), .in17(register_18_q),
    .in18(register_19_q), .in19(register_20_q), .in20(register_21_q), .in21(register_22_q),
    .in22(register_23_q), .in23(register_24_q), .in24(register_25_q), .in25(register_26_q),
    .in26(register_27_q), .in27(register_28_q), .in28(register_29_q), .in29(register_30_q),
    .in30(register_31_q), .in31(register_32_q), .out(Read_Data_2), .sel(Read_Register_2));
endmodule

module Alu_control (
  input  [1:0] ALUop,
  input  [5:0] Funct,
  output [3:0] out_3
);

  wire and_1_out, and_2_out, and_3_out, and_4_out, and_5_out, and_6_out, and_7_out, and_8_out, not_1_out,
       not_2_out, not_3_out, not_4_out, not_5_out, not_6_out, not_7_out, not_8_out, not_9_out, not_10_out,
       not_11_out, not_12_out, not_13_out, not_14_out, not_15_out, not_16_out, not_17_out, not_18_out,
       not_19_out, not_20_out, not_21_out, not_22_out, not_23_out, not_24_out, not_25_out, not_26_out,
       not_27_out;

  not not_1 (not_1_out, Funct[1]);
  not not_2 (not_2_out, Funct[3]);
  not not_3 (not_3_out, Funct[4]);
  not not_4 (not_4_out, Funct[0]);
  not not_5 (not_5_out, Funct[2]);
  not not_6 (not_6_out, Funct[4]);
  not not_7 (not_7_out, Funct[0]);
  not not_8 (not_8_out, Funct[1]);
  not not_9 (not_9_out, Funct[2]);
  not not_10 (not_10_out, Funct[3]);
  not not_11 (not_11_out, Funct[4]);
  not not_12 (not_12_out, Funct[0]);
  not not_13 (not_13_out, Funct[2]);
  not not_14 (not_14_out, Funct[3]);
  not not_15 (not_15_out, Funct[4]);
  not not_16 (not_16_out, Funct[0]);
  not not_17 (not_17_out, Funct[2]);
  not not_18 (not_18_out, Funct[4]);
  not not_19 (not_19_out, ALUop[1]);
  not not_20 (not_20_out, Funct[0]);
  not not_21 (not_21_out, Funct[2]);
  not not_22 (not_22_out, Funct[3]);
  not not_23 (not_23_out, Funct[4]);
  not not_24 (not_24_out, Funct[0]);
  not not_25 (not_25_out, Funct[2]);
  not not_26 (not_26_out, Funct[4]);
  and and_1 (and_1_out, Funct[0], not_1_out, Funct[2], not_2_out, not_3_out, Funct[5], ALUop[1]);
  and and_2 (and_2_out, not_4_out, Funct[1], not_5_out, Funct[3], not_6_out, Funct[5], ALUop[1]);
  and and_3 (and_3_out, not_7_out, not_8_out, not_9_out, not_10_out, not_11_out, Funct[5], ALUop[1]);
  and and_4 (and_4_out, not_12_out, Funct[1], not_13_out, not_14_out, not_15_out, Funct[5], ALUop[1]);
  and and_5 (and_5_out, not_16_out, Funct[1], not_17_out, Funct[3], not_18_out, Funct[5], ALUop[1]);
  and and_6 (and_6_out, ALUop[0], not_19_out);
  and and_7 (and_7_out, not_20_out, Funct[1], not_21_out, not_22_out, not_23_out, Funct[5], ALUop[1]);
  and and_8 (and_8_out, not_24_out, Funct[1], not_25_out, Funct[3], not_26_out, Funct[5], ALUop[1]);
  or or_1 (out_3[0], and_1_out, and_2_out);
  not not_27 (not_27_out, ALUop[1]);
  or or_2 (out_3[1], not_27_out, and_3_out, and_4_out, and_5_out);
  or or_3 (out_3[2], and_6_out, and_7_out, and_8_out);

  assign out_3[3] = 1'b0;
endmodule

module Instruction_Memory (
  input  [31:0] Read_Adress,
  output RegDst,
  output Branch,
  output MemRead,
  output MemtoReg,
  output [1:0] ALUOp,
  output MemWrite,
  output AluSrc,
  output RegWrite,
  output J,
  output [4:0] Intruction,
  output [4:0] Intruction_2,
  output [4:0] out_13,
  output [15:0] Instruction,
  output [25:0] out_15
);

  Control control_1 (
    .in_1(Read_Adress[31:26]), .RegDst(RegDst), .Branch(Branch), .MemRead(MemRead), .MemtoReg(MemtoReg),
    .ALUOp(ALUOp), .MemWrite(MemWrite), .AluSrc(AluSrc), .RegWrite(RegWrite), .J(J));

  assign Instruction = Read_Adress[15:0];
  assign Intruction = Read_Adress[25:21];
  assign Intruction_2 = Read_Adress[20:16];
  assign out_13 = Read_Adress[15:11];
  assign out_15 = Read_Adress[25:0];
endmodule

module PC (
  input  [31:0] in_1,
  input  clk,
  output [31:0] Instruccion,
  output [31:0] out_4
);

  Register_part #(.width(32)) register_1 (.D(in_1), .en(1'b1), .Q(Instruccion), .clk(clk));  // open: clr
  ROM #(.addrWidth(6), .dataWidth(32)) rom_1 (.addr(Instruccion[5:0]), .data(out_4));  // open: sel

  // Notes on the sheet:
  //   contents of rom_1 (hex, n*v repeats v):
  //   24000001 11111111 11111111 11111111 24000001 11111111 11111111 11111111 24210003 11111111 11111111
  //   11111111 10020 11111111 11111111 11111111 ac000000 11111111 11111111 11111111 8c000000 11111111
  //   11111111 11111111 800000c 11111111 11111111 11111111 801820 11111111 11111111 11111111 10220001
  //   11111111 11111111 11111111 800000c ac230004 11111111 11111111 11111111 800003f 22*11111111
endmodule

module Control (
  input  [5:0] in_1,
  output RegDst,
  output Branch,
  output MemRead,
  output MemtoReg,
  output [1:0] ALUOp,
  output MemWrite,
  output AluSrc,
  output RegWrite,
  output J
);

  haro haro_1 (
    .C31(in_1[5]), .C30(in_1[4]), .C29(in_1[3]), .C28(in_1[2]), .c27(in_1[1]), .c26(in_1[0]),
    .RgDest(RegDst), .Branch(Branch), .Read(MemRead), .MemToReg(MemtoReg), .Aluop1(ALUOp[1]),
    .Aluop0(ALUOp[0]), .MemWr(MemWrite), .Alusrc(AluSrc), .RegWrite(RegWrite));
  J_ecuacion j_ecuacion_1 (.in_1(in_1), .out_2(J));
endmodule

module Data_Memory (
  input  MemWrite,
  input  clk,
  input  [31:0] Adress,
  input  [31:0] Write_data,
  input  MemRead,
  output [31:0] out_6
);

  wire and_1_out, not_1_out;

  and and_1 (and_1_out, MemRead, not_1_out);
  RAM #(.addrWidth(6), .dataWidth(32), .bus("separate")) ram_1 (
    .addr(Adress[5:0]), .din(Write_data), .data(out_6), .clk(clk), .ld(and_1_out));  // open: str, sel, clr
  not not_1 (not_1_out, MemWrite);
endmodule

module RegDst_ecuacion (
  input  [5:0] in_1,
  output out_2
);

  wire not_1_out, not_2_out, not_3_out, not_4_out, not_5_out, not_6_out;

  not not_1 (not_1_out, in_1[0]);
  not not_2 (not_2_out, in_1[1]);
  not not_3 (not_3_out, in_1[2]);
  not not_4 (not_4_out, in_1[3]);
  not not_5 (not_5_out, in_1[4]);
  not not_6 (not_6_out, in_1[5]);
  and and_1 (out_2, not_1_out, not_2_out, not_3_out, not_4_out, not_5_out, not_6_out);
endmodule

module J_ecuacion (
  input  [5:0] in_1,
  output out_2
);

  wire not_1_out, not_2_out, not_3_out, not_4_out;

  not not_1 (not_1_out, in_1[2]);
  not not_2 (not_2_out, in_1[3]);
  not not_3 (not_3_out, in_1[4]);
  not not_4 (not_4_out, in_1[5]);
  and and_1 (out_2, in_1[1], not_1_out, not_2_out, not_3_out, not_4_out);
endmodule

module ALU_final (
  input  [31:0] _1,
  input  [31:0] _2,
  input  [1:0] Alu_op,
  input  [5:0] funct,
  output Zero,
  output [31:0] Result
);

  wire [3:0] alu_control_1_out_3;

  Alu_control alu_control_1 (.ALUop(Alu_op), .Funct(funct), .out_3(alu_control_1_out_3));
  ALU_main main_1 (.A(_1), .B(_2), .CONTROL(alu_control_1_out_3), .Zero(Zero), .OUTPUT(Result));
endmodule

module haro (
  input  C31,
  input  C30,
  input  C29,
  input  C28,
  input  c27,
  input  c26,
  output RgDest,
  output Branch,
  output Read,
  output MemToReg,
  output Aluop1,
  output Aluop0,
  output MemWr,
  output Alusrc,
  output RegWrite
);

  wire and_8_out, and_9_out, and_10_out, and_11_out, and_12_out, not_1_out, not_2_out, not_3_out, not_4_out,
       not_5_out, not_6_out, not_7_out, not_8_out, not_9_out, not_10_out, not_11_out, not_12_out, not_13_out,
       not_14_out, not_15_out, not_16_out, not_17_out, not_18_out, not_19_out, not_20_out, not_21_out,
       not_22_out, not_23_out, not_24_out, not_25_out, not_26_out, not_27_out, not_28_out, not_29_out,
       not_30_out, not_31_out, not_32_out, not_33_out, not_34_out, not_35_out, not_36_out, not_37_out,
       not_38_out, not_39_out, not_40_out, not_41_out, not_42_out, not_43_out, not_44_out, not_45_out,
       not_46_out, not_47_out;

  not not_1 (not_1_out, C31);
  not not_2 (not_2_out, C30);
  not not_3 (not_3_out, C29);
  not not_4 (not_4_out, C28);
  not not_5 (not_5_out, c27);
  not not_6 (not_6_out, c26);
  not not_7 (not_7_out, C31);
  not not_8 (not_8_out, C30);
  not not_9 (not_9_out, C29);
  not not_10 (not_10_out, c27);
  not not_11 (not_11_out, c26);
  not not_12 (not_12_out, C30);
  not not_13 (not_13_out, C29);
  not not_14 (not_14_out, C28);
  not not_15 (not_15_out, C30);
  not not_16 (not_16_out, C28);
  not not_17 (not_17_out, C31);
  not not_18 (not_18_out, C30);
  not not_19 (not_19_out, C29);
  not not_20 (not_20_out, C28);
  not not_21 (not_21_out, c26);
  not not_22 (not_22_out, C31);
  not not_23 (not_23_out, C30);
  not not_24 (not_24_out, C29);
  not not_25 (not_25_out, c27);
  not not_26 (not_26_out, c26);
  not not_27 (not_27_out, C30);
  not not_28 (not_28_out, C28);
  not not_29 (not_29_out, C31);
  not not_30 (not_30_out, C30);
  not not_31 (not_31_out, C28);
  not not_32 (not_32_out, c27);
  not not_33 (not_33_out, C30);
  not not_34 (not_34_out, C28);
  not not_35 (not_35_out, C31);
  not not_36 (not_36_out, C30);
  not not_37 (not_37_out, C29);
  not not_38 (not_38_out, C28);
  not not_39 (not_39_out, c27);
  not not_40 (not_40_out, c26);
  not not_41 (not_41_out, C31);
  not not_42 (not_42_out, C30);
  not not_43 (not_43_out, C28);
  not not_44 (not_44_out, c27);
  not not_45 (not_45_out, C30);
  not not_46 (not_46_out, C29);
  not not_47 (not_47_out, C28);
  and and_1 (RgDest, not_1_out, not_2_out, not_3_out, not_4_out, not_5_out, not_6_out);
  and and_2 (Branch, not_7_out, not_8_out, not_9_out, C28, not_10_out, not_11_out);
  and and_3 (Read, C31, not_12_out, not_13_out, not_14_out, c27, c26);
  and and_4 (MemToReg, C31, not_15_out, not_16_out, c27, c26);
  and and_5 (Aluop1, not_17_out, not_18_out, not_19_out, not_20_out, not_21_out);
  and and_6 (Aluop0, not_22_out, not_23_out, not_24_out, C28, not_25_out, not_26_out);
  and and_7 (MemWr, C31, not_27_out, C29, not_28_out, c27, c26);
  and and_8 (and_8_out, not_29_out, not_30_out, C29, not_31_out, not_32_out, c26);
  and and_9 (and_9_out, C31, not_33_out, not_34_out, c27, c26);
  and and_10 (and_10_out, not_35_out, not_36_out, not_37_out, not_38_out, not_39_out, not_40_out);
  and and_11 (and_11_out, not_41_out, not_42_out, C29, not_43_out, not_44_out, c26);
  and and_12 (and_12_out, C31, not_45_out, not_46_out, not_47_out, c27, c26);
  or or_1 (Alusrc, and_8_out, and_9_out);
  or or_2 (RegWrite, and_10_out, and_11_out, and_12_out);
endmodule
