// Logisim project Micro.circ as structural Verilog: 3 circuits, main circuit main
module main (
  input  [7:0] WR_Data,
  input  [2:0] RD_Adress_A,
  input  [2:0] RD_Adress_B,
  input  Enable,
  input  [2:0] WR_Adress,
  output [7:0] RD_Data_A,
  output [7:0] RD_Data_A_2
);

  wire Clock_out;

  Clock Clock (.out(Clock_out));
  Register_Bank register_bank_1 (
    .Clk(Clock_out), .in_5(Enable), .Wr_Adress(WR_Adress), .Wr_Data(WR_Data), .RD_Adress_A(RD_Adress_A),
    .RD_Adress_B(RD_Adress_B), .RD_Data_A(RD_Data_A), .RD_Data_B(RD_Data_A_2));
endmodule

module _8_bit_Register (
  input  [7:0] Input,
  input  Clck,
  input  Enable,
  output [7:0] OutPut
);

  D_Flip_Flop d_ff_1 (.clk(Clck), .D(Input[7]), .Q(OutPut[7]), .en(Enable));  // open: Qn, preset, reset
  D_Flip_Flop d_ff_2 (.clk(Clck), .D(Input[6]), .Q(OutPut[6]), .en(Enable));  // open: Qn, preset, reset
  D_Flip_Flop d_ff_3 (.clk(Clck), .D(Input[5]), .Q(OutPut[5]), .en(Enable));  // open: Qn, preset, reset
  D_Flip_Flop d_ff_4 (.clk(Clck), .D(Input[4]), .Q(OutPut[4]), .en(Enable));  // open: Qn, preset, reset
  D_Flip_Flop d_ff_5 (.clk(Clck), .D(Input[3]), .Q(OutPut[3]), .en(Enable));  // open: Qn, preset, reset
  D_Flip_Flop d_ff_6 (.clk(Clck), .D(Input[2]), .Q(OutPut[2]), .en(Enable));  // open: Qn, preset, reset
  D_Flip_Flop d_ff_7 (.clk(Clck), .D(Input[1]), .Q(OutPut[1]), .en(Enable));  // open: Qn, preset, reset
  D_Flip_Flop d_ff_8 (.clk(Clck), .D(Input[0]), .Q(OutPut[0]), .en(Enable));  // open: Qn, preset, reset
endmodule

module Register_Bank (
  input  [7:0] Wr_Data,
  input  [2:0] RD_Adress_A,
  input  Clk,
  input  [2:0] RD_Adress_B,
  input  in_5,
  input  [2:0] Wr_Adress,
  output [7:0] RD_Data_A,
  output [7:0] RD_Data_B
);

  wire decoder_1_out0, decoder_1_out1, decoder_1_out2, decoder_1_out3, decoder_1_out4, decoder_1_out5,
       decoder_1_out6, decoder_1_out7;
  wire [7:0] n8_bit_register_1_output, n8_bit_register_2_output, n8_bit_register_3_output,
       n8_bit_register_4_output, n8_bit_register_5_output, n8_bit_register_6_output,
       n8_bit_register_7_output, n8_bit_register_8_output;

  Decoder #(.select(3), .disabled(0)) decoder_1 (
    .out0(decoder_1_out0), .out1(decoder_1_out1), .out2(decoder_1_out2), .out3(decoder_1_out3),
    .out4(decoder_1_out4), .out5(decoder_1_out5), .out6(decoder_1_out6), .out7(decoder_1_out7),
    .sel(Wr_Adress), .en(in_5));
  _8_bit_Register u_8_bit_register_1 (
    .Clck(Clk), .Enable(decoder_1_out0), .Input(Wr_Data), .OutPut(n8_bit_register_1_output));
  _8_bit_Register u_8_bit_register_2 (
    .Clck(Clk), .Enable(decoder_1_out1), .Input(Wr_Data), .OutPut(n8_bit_register_2_output));
  _8_bit_Register u_8_bit_register_3 (
    .Clck(Clk), .Enable(decoder_1_out2), .Input(Wr_Data), .OutPut(n8_bit_register_3_output));
  _8_bit_Register u_8_bit_register_4 (
    .Clck(Clk), .Enable(decoder_1_out3), .Input(Wr_Data), .OutPut(n8_bit_register_4_output));
  _8_bit_Register u_8_bit_register_5 (
    .Clck(Clk), .Enable(decoder_1_out4), .Input(Wr_Data), .OutPut(n8_bit_register_5_output));
  _8_bit_Register u_8_bit_register_6 (
    .Clck(Clk), .Enable(decoder_1_out5), .Input(Wr_Data), .OutPut(n8_bit_register_6_output));
  _8_bit_Register u_8_bit_register_7 (
    .Clck(Clk), .Enable(decoder_1_out6), .Input(Wr_Data), .OutPut(n8_bit_register_7_output));
  _8_bit_Register u_8_bit_register_8 (
    .Clck(Clk), .Enable(decoder_1_out7), .Input(Wr_Data), .OutPut(n8_bit_register_8_output));
  Multiplexer #(.select(3), .width(8)) multiplexer_1 (
    .in0(n8_bit_register_1_output), .in1(n8_bit_register_2_output), .in2(n8_bit_register_3_output),
    .in3(n8_bit_register_4_output), .in4(n8_bit_register_5_output), .in5(n8_bit_register_6_output),
    .in6(n8_bit_register_7_output), .in7(n8_bit_register_8_output), .out(RD_Data_A), .sel(RD_Adress_A));  // open: en
  Multiplexer #(.select(3), .width(8)) multiplexer_2 (
    .in0(n8_bit_register_1_output), .in1(n8_bit_register_2_output), .in2(n8_bit_register_3_output),
    .in3(n8_bit_register_4_output), .in4(n8_bit_register_5_output), .in5(n8_bit_register_6_output),
    .in6(n8_bit_register_7_output), .in7(n8_bit_register_8_output), .out(RD_Data_B), .sel(RD_Adress_B));  // open: en
endmodule
