// Logisim project Pacemaker complejo.circ as structural Verilog: 4 circuits, main circuit main
module main (
  input  Superior_Latido,
  input  Inferior_latido,
  output \Superior_señal ,
  output \Inferior_señal ,
  output [5:0] out_5,
  output [5:0] out_6
);

  wire clock_1_out, controller_1_taen, controller_1_tald, controller_1_tven, controller_1_tvld, or_1_out,
       or_2_out, timer_1_tcd, timer_2_tcd;

  Clock clock_1 (.out(clock_1_out));
  or or_1 (or_1_out, controller_1_tald, controller_1_taen);
  Timer timer_1 (
    .rst(1'b0), .Clck(clock_1_out), .UD(1'b1), .Load(controller_1_tald), .En(or_1_out), .TCd(timer_1_tcd),
    .in_6(6'b000100), .Count(out_5));  // open: TCu
  Controller controller_1 (
    .Clck(clock_1_out), .Tald(controller_1_tald), .Taen(controller_1_taen), .Za(timer_1_tcd),
    .Tvld(controller_1_tvld), .Tven(controller_1_tven), .Zv(timer_2_tcd), .Sa(Superior_Latido),
    .Pa(\Superior_señal ), .Sv(Inferior_latido), .PV(\Inferior_señal ));
  or or_2 (or_2_out, controller_1_tvld, controller_1_tven);
  Timer timer_2 (
    .rst(1'b0), .Clck(clock_1_out), .UD(1'b1), .Load(controller_1_tvld), .En(or_2_out), .TCd(timer_2_tcd),
    .in_6(6'b000111), .Count(out_6));  // open: TCu
endmodule

module Timer (
  input  rst,
  input  Clck,
  input  UD,
  input  Load,
  input  En,
  input  [5:0] in_6,
  output TCu,
  output [5:0] Count,
  output TCd
);

  wire not_2_out;
  wire [5:0] adder_1_out, multiplexer_1_out, multiplexer_2_out, not_1_out;

  Multiplexer #(.width(6), .enable("false")) multiplexer_1 (
    .in0(6'b000001), .in1({6{1'b1}}), .out(multiplexer_1_out), .sel(UD));
  Adder #(.width(6)) adder_1 (.a(Count), .b(multiplexer_1_out), .out(adder_1_out));  // open: cin, cout
  Multiplexer #(.width(6), .enable("false")) multiplexer_2 (
    .in0(adder_1_out), .in1(in_6), .out(multiplexer_2_out), .sel(Load));
  Register #(.width(6)) register_1 (.D(multiplexer_2_out), .en(En), .Q(Count), .clk(Clck), .clr(rst));
  assign not_1_out = ~Count;  // NOT_Gate not_1, 6 bits wide
  not not_2 (not_2_out, UD);
  and and_1 (TCu, Count[0], Count[1], Count[2], Count[3], Count[4], Count[5], not_2_out);
  and and_2 (TCd, not_1_out[0], not_1_out[1], not_1_out[2], not_1_out[3], not_1_out[4], not_1_out[5], UD);
endmodule

module FSM (
  input  Clck,
  input  S2,
  input  S1,
  input  S0,
  output S2_2,
  output S1_2,
  output S0_2
);

  D_Flip_Flop d_ff_1 (.clk(Clck), .D(S2), .Q(S2_2), .en(1'b1));  // open: Qn, preset, reset
  D_Flip_Flop d_ff_2 (.clk(Clck), .D(S1), .Q(S1_2), .en(1'b1));  // open: Qn, preset, reset
  D_Flip_Flop d_ff_3 (.clk(Clck), .D(S0), .Q(S0_2), .en(1'b1));  // open: Qn, preset, reset
endmodule

module Controller (
  input  Za,
  input  Zv,
  input  Sa,
  input  Sv,
  input  Clck,
  output Pa,
  output Tald,
  output Taen,
  output PV,
  output Tvld,
  output Tven
);

  wire and_1_out, and_2_out, and_3_out, and_4_out, and_5_out, and_6_out, and_7_out, and_8_out, and_9_out,
       and_10_out, fsm_1_s0_2, fsm_1_s1_2, fsm_1_s2_2, not_1_out, not_2_out, not_3_out, not_4_out, not_5_out,
       not_6_out, not_7_out, not_8_out, not_9_out, not_10_out, not_11_out, not_12_out, not_13_out,
       not_14_out, not_15_out, not_16_out, not_17_out, not_18_out, not_19_out, not_20_out, not_21_out,
       not_22_out, not_23_out, not_24_out, not_25_out, not_26_out, not_27_out, not_28_out, not_29_out,
       not_30_out, not_31_out, not_32_out, not_33_out, not_34_out, not_35_out, not_36_out, S0_out, S1_out,
       S2_out;

  FSM fsm_1 (
    .Clck(Clck), .S2_2(fsm_1_s2_2), .S1_2(fsm_1_s1_2), .S0_2(fsm_1_s0_2), .S2(S2_out), .S1(S1_out),
    .S0(S0_out));
  not not_1 (not_1_out, fsm_1_s2_2);
  not not_2 (not_2_out, fsm_1_s1_2);
  not not_3 (not_3_out, fsm_1_s0_2);
  not not_4 (not_4_out, Za);
  not not_5 (not_5_out, Sv);
  not not_6 (not_6_out, fsm_1_s1_2);
  not not_7 (not_7_out, fsm_1_s0_2);
  not not_8 (not_8_out, Sv);
  not not_9 (not_9_out, fsm_1_s2_2);
  not not_10 (not_10_out, fsm_1_s0_2);
  not not_11 (not_11_out, fsm_1_s2_2);
  not not_12 (not_12_out, fsm_1_s1_2);
  not not_13 (not_13_out, fsm_1_s2_2);
  not not_14 (not_14_out, fsm_1_s1_2);
  not not_15 (not_15_out, fsm_1_s2_2);
  not not_16 (not_16_out, fsm_1_s1_2);
  not not_17 (not_17_out, fsm_1_s0_2);
  not not_18 (not_18_out, fsm_1_s2_2);
  not not_19 (not_19_out, fsm_1_s1_2);
  not not_20 (not_20_out, Za);
  not not_21 (not_21_out, fsm_1_s2_2);
  not not_22 (not_22_out, fsm_1_s0_2);
  not not_23 (not_23_out, fsm_1_s1_2);
  not not_24 (not_24_out, fsm_1_s0_2);
  not not_25 (not_25_out, Sv);
  not not_26 (not_26_out, fsm_1_s2_2);
  not not_27 (not_27_out, fsm_1_s0_2);
  not not_28 (not_28_out, fsm_1_s2_2);
  not not_29 (not_29_out, fsm_1_s1_2);
  not not_30 (not_30_out, fsm_1_s0_2);
  not not_31 (not_31_out, fsm_1_s2_2);
  not not_32 (not_32_out, fsm_1_s1_2);
  not not_33 (not_33_out, fsm_1_s1_2);
  not not_34 (not_34_out, fsm_1_s2_2);
  not not_35 (not_35_out, fsm_1_s1_2);
  not not_36 (not_36_out, fsm_1_s0_2);
  and and_1 (and_1_out, not_1_out, fsm_1_s1_2, fsm_1_s0_2);
  and and_2 (and_2_out, fsm_1_s2_2, not_2_out, not_3_out, not_4_out, not_5_out);
  and and_3 (and_3_out, fsm_1_s2_2, not_6_out, not_7_out, Za, not_8_out);
  and and_4 (and_4_out, not_9_out, fsm_1_s1_2, not_10_out);
  and and_5 (and_5_out, not_11_out, not_12_out, fsm_1_s0_2, Sa);
  and and_6 (and_6_out, not_13_out, not_14_out, fsm_1_s0_2, Za);
  and and_7 (and_7_out, not_15_out, not_16_out, not_17_out);
  and and_8 (and_8_out, not_18_out, not_19_out, not_20_out);
  and and_9 (and_9_out, not_21_out, fsm_1_s1_2, not_22_out);
  and and_10 (and_10_out, fsm_1_s2_2, not_23_out, not_24_out, not_25_out, Zv);
  and u_Pa (Pa, not_26_out, fsm_1_s1_2, not_27_out);
  and u_Tald (Tald, not_28_out, not_29_out, not_30_out);
  and u_Taen (Taen, not_31_out, not_32_out, fsm_1_s0_2);
  and u_Pv (PV, fsm_1_s2_2, not_33_out, fsm_1_s0_2);
  and u_TVld (Tvld, not_34_out, fsm_1_s1_2, fsm_1_s0_2);
  and u_Tven (Tven, fsm_1_s2_2, not_35_out, not_36_out);
  or S2 (S2_out, and_1_out, and_2_out, and_3_out);
  or S1 (S1_out, and_4_out, and_5_out, and_6_out);
  or S0 (S0_out, and_7_out, and_8_out, and_9_out, and_10_out);
endmodule
