// Logisim project Pacemaker sencillo.circ as structural Verilog: 4 circuits, main circuit main
module main (
  input  \Latido_de_corazón ,
  output [5:0] out_2,
  output \Pulso_al_corazón 
);

  wire clock_1_out, controller_pacemaker_sencillo_1_c, controller_pacemaker_sencillo_1_t, or_1_out,
       timer_1_tcd;

  Clock clock_1 (.out(clock_1_out));
  Controller_Pacemaker_sencillo controller_pacemaker_sencillo_1 (
    .S(\Latido_de_corazón ), .Z(timer_1_tcd), .Clck(clock_1_out), .t(controller_pacemaker_sencillo_1_t),
    .P(\Pulso_al_corazón ), .C(controller_pacemaker_sencillo_1_c));
  or or_1 (or_1_out, controller_pacemaker_sencillo_1_t, controller_pacemaker_sencillo_1_c);
  Timer timer_1 (
    .UD(1'b1), .En(or_1_out), .Load(controller_pacemaker_sencillo_1_t), .in_6(6'b011001), .Clck(clock_1_out),
    .Count(out_2), .TCd(timer_1_tcd));  // open: rst, TCu
endmodule

module Timer (
  input  Clck,
  input  rst,
  input  UD,
  input  En,
  input  Load,
  input  [5:0] in_6,
  output TCu,
  output [5:0] Count,
  output TCd
);

  wire not_2_out;
  wire [5:0] adder_1_out, multiplexer_1_out, multiplexer_2_out, not_1_out;

  Multiplexer #(.width(6), .enable("false")) multiplexer_1 (
    .in0(6'b000001), .in1({6{1'b1}}), .out(multiplexer_1_out), .sel(UD));
  Adder #(.width(6)) adder_1 (.a(Count), .b(multiplexer_1_out), .out(adder_1_out));  // open: cin, cout
  Multiplexer #(.width(6), .enable("false")) multiplexer_2 (
    .in0(adder_1_out), .in1(in_6), .out(multiplexer_2_out), .sel(Load));
  Register #(.width(6)) register_1 (.D(multiplexer_2_out), .en(En), .Q(Count), .clk(Clck), .clr(rst));
  assign not_1_out = ~Count;  // NOT_Gate not_1, 6 bits wide
  not not_2 (not_2_out, UD);
  and and_1 (TCu, Count[0], Count[1], Count[2], Count[3], Count[4], Count[5], not_2_out);
  and and_2 (TCd, not_1_out[0], not_1_out[1], not_1_out[2], not_1_out[3], not_1_out[4], not_1_out[5], UD);
endmodule

module Controller_Pacemaker_sencillo (
  input  Clck,
  input  S,
  input  Z,
  output t,
  output P,
  output C
);

  wire and_4_out, and_5_out, and_6_out, fsm_1_s0_2, fsm_1_s1_2, not_1_out, not_2_out, not_3_out, not_4_out,
       not_5_out, not_6_out, not_7_out, not_8_out, not_9_out, not_10_out, not_11_out, or_1_out;

  FSM fsm_1 (.Clck(Clck), .S1_2(fsm_1_s1_2), .S0_2(fsm_1_s0_2), .S1(and_4_out), .S0(or_1_out));
  not not_1 (not_1_out, S);
  not not_2 (not_2_out, Z);
  not not_3 (not_3_out, fsm_1_s1_2);
  not not_4 (not_4_out, fsm_1_s1_2);
  not not_5 (not_5_out, fsm_1_s0_2);
  not not_6 (not_6_out, fsm_1_s1_2);
  not not_7 (not_7_out, fsm_1_s0_2);
  not not_8 (not_8_out, fsm_1_s0_2);
  not not_9 (not_9_out, fsm_1_s1_2);
  not not_10 (not_10_out, S);
  not not_11 (not_11_out, fsm_1_s1_2);
  and and_1 (t, not_6_out, not_7_out);
  and and_2 (P, fsm_1_s1_2, not_8_out);
  and and_3 (C, not_9_out, fsm_1_s0_2);
  and and_4 (and_4_out, not_10_out, Z, not_11_out, fsm_1_s0_2);
  and and_5 (and_5_out, not_1_out, not_2_out, not_3_out);
  and and_6 (and_6_out, not_4_out, not_5_out);
  or or_1 (or_1_out, and_5_out, and_6_out);
endmodule

module FSM (
  input  Clck,
  input  S1,
  input  S0,
  output S1_2,
  output S0_2
);

  D_Flip_Flop d_ff_1 (.clk(Clck), .D(S1), .Q(S1_2), .en(1'b1));  // open: Qn, preset, reset
  D_Flip_Flop d_ff_2 (.clk(Clck), .D(S0), .Q(S0_2), .en(1'b1));  // open: Qn, preset, reset
endmodule
