// Logisim project Recoder.circ as structural Verilog: 3 circuits, main circuit main
module main (
  input  [7:0] Input,
  input  shr_in,
  input  shl_in,
  input  [2:0] Control,
  output [7:0] Output
);

  wire clock_1_out;
  wire [1:0] combinational_circuit_1_output;

  Clock clock_1 (.out(clock_1_out));
  completo completo_1 (
    .shr_in(shr_in), .Selector(combinational_circuit_1_output), .in_5(clock_1_out), .enable(1'b1),
    .Input(Input), .Output(Output), .shl_in(shl_in));
  Combinational_circuit combinational_circuit_1 (.Input(Control), .Output(combinational_circuit_1_output));
endmodule

module completo (
  input  [7:0] Input,
  input  shr_in,
  input  shl_in,
  input  [1:0] Selector,
  input  in_5,
  input  enable,
  output [7:0] Output
);

  wire multiplexer_1_out, multiplexer_2_out, multiplexer_3_out, multiplexer_4_out, multiplexer_5_out,
       multiplexer_6_out, multiplexer_7_out, multiplexer_8_out;

  Multiplexer #(.select(2)) multiplexer_1 (
    .in0(Output[7]), .in1(Input[7]), .in2(shr_in), .in3(Output[6]), .out(multiplexer_1_out), .sel(Selector));  // open: en
  Multiplexer #(.select(2)) multiplexer_2 (
    .in0(Output[6]), .in1(Input[6]), .in2(Output[7]), .in3(Output[5]), .out(multiplexer_2_out), .sel(Selector));  // open: en
  D_Flip_Flop d_ff_1 (.clk(in_5), .D(multiplexer_1_out), .Q(Output[7]), .en(enable));  // open: Qn, preset, reset
  Multiplexer #(.select(2)) multiplexer_3 (
    .in0(Output[5]), .in1(Input[5]), .in2(Output[6]), .in3(Output[4]), .out(multiplexer_3_out), .sel(Selector));  // open: en
  D_Flip_Flop d_ff_2 (.clk(in_5), .D(multiplexer_2_out), .Q(Output[6]), .en(enable));  // open: Qn, preset, reset
  Multiplexer #(.select(2)) multiplexer_4 (
    .in0(Output[4]), .in1(Input[4]), .in2(Output[5]), .in3(Output[3]), .out(multiplexer_4_out), .sel(Selector));  // open: en
  D_Flip_Flop d_ff_3 (.clk(in_5), .D(multiplexer_3_out), .Q(Output[5]), .en(enable));  // open: Qn, preset, reset
  Multiplexer #(.select(2)) multiplexer_5 (
    .in0(Output[3]), .in1(Input[3]), .in2(Output[4]), .in3(Output[2]), .out(multiplexer_5_out), .sel(Selector));  // open: en
  D_Flip_Flop d_ff_4 (.clk(in_5), .D(multiplexer_4_out), .Q(Output[4]), .en(enable));  // open: Qn, preset, reset
  Multiplexer #(.select(2)) multiplexer_6 (
    .in0(Output[2]), .in1(Input[2]), .in2(Output[3]), .in3(Output[1]), .out(multiplexer_6_out), .sel(Selector));  // open: en
  D_Flip_Flop d_ff_5 (.clk(in_5), .D(multiplexer_5_out), .Q(Output[3]), .en(enable));  // open: Qn, preset, reset
  Multiplexer #(.select(2)) multiplexer_7 (
    .in0(Output[1]), .in1(Input[1]), .in2(Output[2]), .in3(Output[0]), .out(multiplexer_7_out), .sel(Selector));  // open: en
  D_Flip_Flop d_ff_6 (.clk(in_5), .D(multiplexer_6_out), .Q(Output[2]), .en(enable));  // open: Qn, preset, reset
  Multiplexer #(.select(2)) multiplexer_8 (
    .in0(Output[0]), .in1(Input[0]), .in2(Output[1]), .in3(shl_in), .out(multiplexer_8_out), .sel(Selector));  // open: en
  D_Flip_Flop d_ff_7 (.clk(in_5), .D(multiplexer_7_out), .Q(Output[1]), .en(enable));  // open: Qn, preset, reset
  D_Flip_Flop d_ff_8 (.clk(in_5), .D(multiplexer_8_out), .Q(Output[0]), .en(enable));  // open: Qn, preset, reset
endmodule

module Combinational_circuit (
  input  [2:0] Input,
  output [1:0] Output
);

  wire not_1_out, not_2_out, not_3_out, not_4_out, not_5_out, not_6_out;
  wire [2:0] and_1_out;

  not not_1 (not_1_out, Input[0]);
  and and_1 (and_1_out[0], not_1_out, not_2_out, not_3_out);
  not not_2 (not_2_out, Input[1]);
  not not_3 (not_3_out, Input[2]);
  and and_2 (and_1_out[1], Input[0], not_4_out, not_5_out);
  not not_4 (not_4_out, Input[1]);
  not not_5 (not_5_out, Input[2]);
  and and_3 (and_1_out[2], Input[1], not_6_out);
  not not_6 (not_6_out, Input[2]);
  Multiplexer #(.select(4), .width(2)) multiplexer_1 (
    .in1(2'b00), .in2(2'b11), .in4(2'b10), .in8(2'b01), .out(Output), .sel({Input[2], and_1_out}));  // open: in0, in3, in5, in6, in7, in9, in10, in11, in12, in13, in14, in15, en
endmodule
