// Logisim project Secuencia 4 bits.circ as structural Verilog: 4 circuits, main circuit main
module main (
);

  wire secuencia_2_1_o0, secuencia_2_1_o1, secuencia_2_1_o2, secuencia_2_1_o3;

  Secuencia_2 secuencia_2_1 (
    .O3(secuencia_2_1_o3), .O2(secuencia_2_1_o2), .O1(secuencia_2_1_o1), .O0(secuencia_2_1_o0));
  LED led_1 (.in(secuencia_2_1_o2));
  LED led_2 (.in(secuencia_2_1_o3));
  LED led_3 (.in(secuencia_2_1_o0));
  LED led_4 (.in(secuencia_2_1_o1));
endmodule

module FSM (
  input  Clck,
  input  S1,
  input  S0,
  output S1_2,
  output S0_2
);

  D_Flip_Flop d_ff_1 (.clk(Clck), .D(S1), .Q(S1_2));  // open: Qn, preset, en, reset
  D_Flip_Flop d_ff_2 (.clk(Clck), .D(S0), .Q(S0_2));  // open: Qn, preset, en, reset
endmodule

module Secuencia (
  output [3:0] Output
);

  wire and_1_out, and_2_out, and_3_out, and_4_out, clock_1_out, not_1_out, not_2_out, not_3_out, not_4_out,
       not_5_out, or_1_out, or_2_out;
  wire [1:0] fsm_1_s0_2;

  Clock clock_1 (.out(clock_1_out));
  FSM fsm_1 (.Clck(clock_1_out), .S1_2(fsm_1_s0_2[1]), .S0_2(fsm_1_s0_2[0]), .S1(or_1_out), .S0(or_2_out));
  Multiplexer #(.select(2), .width(4)) multiplexer_1 (
    .in0(4'b0001), .in1(4'b0011), .in2(4'b1100), .in3(4'b1000), .out(Output), .sel(fsm_1_s0_2));  // open: en
  not not_1 (not_1_out, fsm_1_s0_2[0]);
  not not_2 (not_2_out, fsm_1_s0_2[1]);
  not not_3 (not_3_out, fsm_1_s0_2[0]);
  not not_4 (not_4_out, fsm_1_s0_2[1]);
  not not_5 (not_5_out, fsm_1_s0_2[0]);
  and and_1 (and_1_out, fsm_1_s0_2[1], not_1_out);
  and and_2 (and_2_out, not_2_out, fsm_1_s0_2[0]);
  and and_3 (and_3_out, fsm_1_s0_2[1], not_3_out);
  and and_4 (and_4_out, not_4_out, not_5_out);
  LED ld3 (.in(Output[3]));
  or or_1 (or_1_out, and_1_out, and_2_out);
  or or_2 (or_2_out, and_3_out, and_4_out);
  LED ld2 (.in(Output[2]));
  LED ld1 (.in(Output[1]));
  LED ld0 (.in(Output[0]));
endmodule

module Secuencia_2 (
  output O3,
  output O2,
  output O1,
  output O0
);

  wire and_1_out, and_2_out, and_3_out, and_4_out, clock_1_out, not_1_out, not_2_out, not_3_out, not_4_out,
       not_5_out, or_1_out, or_2_out;
  wire [1:0] fsm_1_s0_2;

  Clock clock_1 (.out(clock_1_out));
  FSM fsm_1 (.Clck(clock_1_out), .S1_2(fsm_1_s0_2[1]), .S0_2(fsm_1_s0_2[0]), .S1(or_1_out), .S0(or_2_out));
  Multiplexer #(.select(2), .width(4)) multiplexer_1 (
    .in0(4'b0001), .in1(4'b0011), .in2(4'b1100), .in3(4'b1000), .out({O3, O2, O1, O0}), .sel(fsm_1_s0_2));  // open: en
  not not_1 (not_1_out, fsm_1_s0_2[0]);
  not not_2 (not_2_out, fsm_1_s0_2[1]);
  not not_3 (not_3_out, fsm_1_s0_2[0]);
  not not_4 (not_4_out, fsm_1_s0_2[1]);
  not not_5 (not_5_out, fsm_1_s0_2[0]);
  and and_1 (and_1_out, fsm_1_s0_2[1], not_1_out);
  and and_2 (and_2_out, not_2_out, fsm_1_s0_2[0]);
  and and_3 (and_3_out, fsm_1_s0_2[1], not_3_out);
  and and_4 (and_4_out, not_4_out, not_5_out);
  or or_1 (or_1_out, and_1_out, and_2_out);
  or or_2 (or_2_out, and_3_out, and_4_out);
endmodule
